// Logisim project Group2.circ as structural Verilog
module AU (
  input  [15:0] A,
  input  [15:0] B,
  input  [3:0] selector,
  output [7:0] result
);

  BitAdder bitadder_1 ();  // open: in0, out
  Adder adder_1 ();  // open: a, b, out, cin, cout
  Multiplexer #(.select(4), .width(8)) multiplexer_1 (.sel(selector));  // open: in0, in1, in2, in3, in4, in5, in6, in7, in8, in9, in10, in11, in12, in13, in14, in15, out
endmodule
